// Logisim project automat_bancar_psn.circ as structural Verilog
module main (
  input  [3:0] Input_bus_1,
  input  [3:0] Input_bus_2,
  input  [3:0] Input_bus_3,
  input  Input_2,
  input  [3:0] Input_bus_4,
  input  Input_3,
  input  Input_4,
  input  [3:0] Input_bus_5,
  input  [1:0] Input_bus_6,
  input  [3:0] Input_bus_7,
  input  Input_5,
  input  Input_6,
  input  Input_7,
  input  Input_8,
  input  [3:0] Input_bus_8,
  input  Input_9,
  input  [3:0] Input_bus_9,
  input  Input_10,
  input  [3:0] Input_bus_10,
  input  Input_11,
  input  [3:0] Input_bus_11,
  input  [3:0] Input_bus_12,
  input  [3:0] Input_bus_13,
  input  [3:0] Input_bus_14,
  input  [3:0] Input_bus_15,
  input  Input_12,
  input  Input_13,
  input  Input_14,
  output Output_1,
  output [9:0] out_30,
  output Output_2,
  output [6:0] Output_bus_1,
  output [3:0] Output_bus_2
);

  wire algoritm_bancnote_1_confirm, clock_1_out, comparator_suma_1_confirmare, decodificator_afisor_1_final,
       demux_alta_operatie_1_alta_operatie, demux_selectare_operatie_1_enable_afisare,
       demux_selectare_operatie_1_enable_depunere, demux_selectare_operatie_1_enable_retragere,
       demux_selectare_operatie_1_enable_schimbare, memorie_bancnote_1_final_mem_ad,
       memorie_bancnote_1_final_mem_sc, memorie_bancnote_1_final_tr, memorie_cont_1_final_mem_ad,
       memorie_cont_1_final_mem_sc, memorie_cont_1_final_mem_schimbare, scazator_bancnote_1_final,
       scazator_bancnote_2_final, scazator_bancnote_3_final, scazator_bancnote_4_final,
       scazator_sold_1_final_scazator, sumator_bancnote_1_final, sumator_bancnote_2_final,
       sumator_bancnote_3_final, sumator_bancnote_4_final, sumator_sold_1_final_sumator,
       transformator_suma_1_final_trans_suma, transformator_suma_2_final_trans_suma,
       uc_1_enable_adunare_banc, uc_1_enable_adunare_sold, uc_1_enable_algoritm, uc_1_enable_comparator,
       uc_1_enable_demux_alta_op, uc_1_enable_nr10, uc_1_enable_nr50, uc_1_enable_nr100, uc_1_enable_nr500,
       uc_1_enable_operatie, uc_1_enable_pin, uc_1_enable_scadere_banc, uc_1_enable_scadere_sold,
       uc_1_enable_scazator, uc_1_enable_scazator10, uc_1_enable_scazator50, uc_1_enable_scazator100,
       uc_1_enable_scazator500, uc_1_enable_sum10, uc_1_enable_sum50, uc_1_enable_sum100, uc_1_enable_sum500,
       uc_1_enable_suma, uc_1_enable_transmitere;
  wire [1:0] numarator_afisor_1_numar;
  wire [3:0] algoritm_bancnote_1_b10_out, algoritm_bancnote_1_b50_out, algoritm_bancnote_1_b100_out,
       algoritm_bancnote_1_b500_out, memorie_bancnote_1_nr10nou, memorie_bancnote_1_nr50_nou,
       memorie_bancnote_1_nr100_nou, memorie_bancnote_1_nr500_curent, mux_afisor_1_catod,
       registru_actualizare_bancnote_1_bancnote_out, registru_actualizare_bancnote_2_bancnote_out,
       registru_actualizare_bancnote_3_bancnote_out, registru_actualizare_bancnote_4_bancnote_out,
       registru_incarcare_pin_1_pin_out, scazator_bancnote_1_bancnote_finale,
       scazator_bancnote_2_bancnote_finale, scazator_bancnote_3_bancnote_finale,
       scazator_bancnote_4_bancnote_finale, sumator_bancnote_1_bancnote_finale,
       sumator_bancnote_2_bancnote_finale, sumator_bancnote_3_bancnote_finale,
       sumator_bancnote_4_bancnote_finale, transformator_cifre_1_mii, transformator_cifre_1_sute,
       transformator_cifre_1_unitati, transformator_cifre_1_zeci;
  wire [9:0] registru_suma_1_suma_out, scazator_sold_1_suma_finala, sumator_sold_1_suma_finala,
       transformator_suma_1_suma, transformator_suma_2_suma, undriven;

  Clock clock_1 (.out(clock_1_out));
  registru_actualizare_bancnote registru_actualizare_bancnote_1 (
    .bancnote_in(Input_bus_7), .clk(clock_1_out), .reset(Input_2), .enable(uc_1_enable_nr500),
    .validare(Input_7), .bancnote_out(registru_actualizare_bancnote_1_bancnote_out));
  registru_actualizare_bancnote registru_actualizare_bancnote_2 (
    .bancnote_in(Input_bus_9), .clk(clock_1_out), .reset(Input_2), .enable(uc_1_enable_nr100),
    .validare(Input_10), .bancnote_out(registru_actualizare_bancnote_2_bancnote_out));
  registru_actualizare_bancnote registru_actualizare_bancnote_3 (
    .bancnote_in(Input_bus_10), .clk(clock_1_out), .reset(Input_2), .enable(uc_1_enable_nr50),
    .validare(Input_11), .bancnote_out(registru_actualizare_bancnote_3_bancnote_out));
  registru_actualizare_bancnote registru_actualizare_bancnote_4 (
    .bancnote_in(Input_bus_13), .clk(clock_1_out), .reset(Input_2), .enable(uc_1_enable_nr10),
    .validare(Input_12), .bancnote_out(registru_actualizare_bancnote_4_bancnote_out));
  sumator_bancnote sumator_bancnote_1 (
    .bancnote_depuse(registru_actualizare_bancnote_1_bancnote_out), .validare(uc_1_enable_sum500),
    .bancnote_initiale(memorie_bancnote_1_nr500_curent),
    .bancnote_finale(sumator_bancnote_1_bancnote_finale), .\final (sumator_bancnote_1_final));
  sumator_bancnote sumator_bancnote_2 (
    .bancnote_depuse(registru_actualizare_bancnote_2_bancnote_out), .validare(uc_1_enable_sum100),
    .bancnote_initiale(memorie_bancnote_1_nr100_nou), .bancnote_finale(sumator_bancnote_2_bancnote_finale),
    .\final (sumator_bancnote_2_final));
  sumator_bancnote sumator_bancnote_3 (
    .bancnote_depuse(registru_actualizare_bancnote_3_bancnote_out), .validare(uc_1_enable_sum50),
    .bancnote_initiale(memorie_bancnote_1_nr50_nou), .bancnote_finale(sumator_bancnote_3_bancnote_finale),
    .\final (sumator_bancnote_3_final));
  sumator_bancnote sumator_bancnote_4 (
    .bancnote_depuse(registru_actualizare_bancnote_4_bancnote_out), .validare(uc_1_enable_sum10),
    .bancnote_initiale(memorie_bancnote_1_nr10nou), .bancnote_finale(sumator_bancnote_4_bancnote_finale),
    .\final (sumator_bancnote_4_final));
  uc uc_1 (
    .clk(clock_1_out), .reset(Input_2), .start(Input_3), .final_mem_banc_sc(memorie_bancnote_1_final_mem_sc),
    .enable_alta_op(demux_alta_operatie_1_alta_operatie),
    .final_schimbare(memorie_cont_1_final_mem_schimbare), .final_sc_banc500(scazator_bancnote_1_final),
    .final_sc_banc100(scazator_bancnote_2_final), .final_sc_banc50(scazator_bancnote_3_final),
    .final_sc_banc10(scazator_bancnote_4_final), .fin_mem_sc(memorie_cont_1_final_mem_sc),
    .confirm_algoritm(algoritm_bancnote_1_confirm), .final_transmitere(memorie_bancnote_1_final_tr),
    .confirm_comparator(comparator_suma_1_confirmare), .final_numarare500(Input_7),
    .final_numarare100(Input_10), .final_numarare50(Input_11), .final_numarare10(Input_12),
    .final_scazator_sold(scazator_sold_1_final_scazator),
    .final_mem_banc_ad(memorie_bancnote_1_final_mem_ad), .final_mem_ad(memorie_cont_1_final_mem_ad),
    .final_sumator_banc500(sumator_bancnote_1_final), .final_sumator_banc100(sumator_bancnote_2_final),
    .final_sumator_banc50(sumator_bancnote_3_final), .final_sumator_banc10(sumator_bancnote_4_final),
    .final_sumator_sold(sumator_sold_1_final_sumator),
    .final_trans_suma_sc(transformator_suma_1_final_trans_suma),
    .final_trans_suma_ad(transformator_suma_2_final_trans_suma), .validare_pin(Input_6),
    .finalizare_sel_op(Input_8), .enable_afisare(demux_selectare_operatie_1_enable_afisare),
    .enable_depunere(demux_selectare_operatie_1_enable_depunere),
    .enable_retragere(demux_selectare_operatie_1_enable_retragere),
    .enable_schimbare(demux_selectare_operatie_1_enable_schimbare),
    .finalizare_afisare(decodificator_afisor_1_final), .led_final(Output_1),
    .enable_demux_alta_op(uc_1_enable_demux_alta_op), .enable_scadere_banc(uc_1_enable_scadere_banc),
    .enable_scazator500(uc_1_enable_scazator500), .enable_scazator100(uc_1_enable_scazator100),
    .enable_scazator50(uc_1_enable_scazator50), .enable_scazator10(uc_1_enable_scazator10),
    .enable_scadere_sold(uc_1_enable_scadere_sold), .enable_scazator(uc_1_enable_scazator),
    .enable_algoritm(uc_1_enable_algoritm), .enable_transmitere(uc_1_enable_transmitere),
    .enable_comparator(uc_1_enable_comparator), .enable_adunare_banc(uc_1_enable_adunare_banc),
    .enable_pin(uc_1_enable_pin), .enable_suma(uc_1_enable_suma),
    .enable_adunare_sold(uc_1_enable_adunare_sold), .enable_operatie(uc_1_enable_operatie),
    .enable_sum500(uc_1_enable_sum500), .enable_sum100(uc_1_enable_sum100), .enable_sum50(uc_1_enable_sum50),
    .enable_sum10(uc_1_enable_sum10), .enable_nr500(uc_1_enable_nr500), .enable_nr100(uc_1_enable_nr100),
    .enable_nr50(uc_1_enable_nr50), .enable_nr10(uc_1_enable_nr10));
  transformator_suma transformator_suma_1 (
    .mii(Input_bus_1), .sute(Input_bus_2), .zeci(Input_bus_3), .unitati(Input_bus_4),
    .enable(demux_selectare_operatie_1_enable_retragere), .validare(Input_4),
    .suma(transformator_suma_1_suma), .final_trans_suma(transformator_suma_1_final_trans_suma));
  registru_incarcare_pin registru_incarcare_pin_1 (
    .pin_in(Input_bus_5), .enable(uc_1_enable_pin), .clk(clock_1_out), .reset(Input_2),
    .pin_out(registru_incarcare_pin_1_pin_out));
  demux_selectare_operatie demux_selectare_operatie_1 (
    .sel(Input_bus_6), .enable(uc_1_enable_operatie), .validare(Input_8),
    .enable_afisare(demux_selectare_operatie_1_enable_afisare),
    .enable_depunere(demux_selectare_operatie_1_enable_depunere),
    .enable_retragere(demux_selectare_operatie_1_enable_retragere),
    .enable_schimbare(demux_selectare_operatie_1_enable_schimbare));
  transformator_suma transformator_suma_2 (
    .mii(Input_bus_11), .sute(Input_bus_12), .zeci(Input_bus_14), .unitati(Input_bus_15),
    .enable(demux_selectare_operatie_1_enable_depunere), .validare(Input_13),
    .suma(transformator_suma_2_suma), .final_trans_suma(transformator_suma_2_final_trans_suma));
  memorie_bancnote memorie_bancnote_1 (
    .clk(clock_1_out), .enable_adunare(uc_1_enable_adunare_banc), .enable_scadere(uc_1_enable_scadere_banc),
    .enable_transmitere(uc_1_enable_transmitere), .nr500_ad(sumator_bancnote_1_bancnote_finale),
    .nr100_ad(sumator_bancnote_2_bancnote_finale), .nr50_ad(sumator_bancnote_3_bancnote_finale),
    .nr10_ad(sumator_bancnote_4_bancnote_finale), .nr500_sc(scazator_bancnote_1_bancnote_finale),
    .nr100_sc(scazator_bancnote_2_bancnote_finale), .nr50_sc(scazator_bancnote_3_bancnote_finale),
    .nr10_sc(scazator_bancnote_4_bancnote_finale), .nr500_curent(memorie_bancnote_1_nr500_curent),
    .nr100_nou(memorie_bancnote_1_nr100_nou), .nr50_nou(memorie_bancnote_1_nr50_nou),
    .nr10nou(memorie_bancnote_1_nr10nou), .final_mem_ad(memorie_bancnote_1_final_mem_ad),
    .final_mem_sc(memorie_bancnote_1_final_mem_sc), .final_tr(memorie_bancnote_1_final_tr));
  comparator_suma comparator_suma_1 (
    .suma_retragere(transformator_suma_1_suma), .suma_cont(registru_suma_1_suma_out),
    .enable(uc_1_enable_comparator), .confirmare(comparator_suma_1_confirmare));
  algoritm_bancnote algoritm_bancnote_1 (
    .suma(transformator_suma_1_suma), .enable(uc_1_enable_algoritm),
    .b500_in(memorie_bancnote_1_nr500_curent), .b100_in(memorie_bancnote_1_nr100_nou),
    .b50_in(memorie_bancnote_1_nr50_nou), .b10_in(memorie_bancnote_1_nr10nou),
    .b500_out(algoritm_bancnote_1_b500_out), .b100_out(algoritm_bancnote_1_b100_out),
    .b50_out(algoritm_bancnote_1_b50_out), .b10_out(algoritm_bancnote_1_b10_out),
    .confirm(algoritm_bancnote_1_confirm));
  sumator_sold sumator_sold_1 (
    .suma_depusa(transformator_suma_2_suma), .validare(uc_1_enable_suma),
    .suma_initiala(registru_suma_1_suma_out), .suma_finala(sumator_sold_1_suma_finala),
    .final_sumator(sumator_sold_1_final_sumator));
  memorie_cont memorie_cont_1 (
    .pin_vechi(registru_incarcare_pin_1_pin_out), .clk(clock_1_out),
    .enable_schimbare_pin(demux_selectare_operatie_1_enable_schimbare),
    .enable_adunare_sold(uc_1_enable_adunare_sold), .enable_scadere_sold(uc_1_enable_scadere_sold),
    .enable_transmitere_sold(Input_5), .suma_adunare(sumator_sold_1_suma_finala),
    .suma_scadere(scazator_sold_1_suma_finala), .pin_nou(Input_bus_8), .validare_pin(Input_9), .sold(out_30),
    .final_mem_sc(memorie_cont_1_final_mem_sc), .final_mem_ad(memorie_cont_1_final_mem_ad),
    .final_mem_schimbare(memorie_cont_1_final_mem_schimbare));
  transformator_cifre transformator_cifre_1 (
    .suma(registru_suma_1_suma_out), .enable(demux_selectare_operatie_1_enable_afisare),
    .mii(transformator_cifre_1_mii), .sute(transformator_cifre_1_sute), .zeci(transformator_cifre_1_zeci),
    .unitati(transformator_cifre_1_unitati));
  demux_alta_operatie demux_alta_operatie_1 (
    .enable(uc_1_enable_demux_alta_op), .sel(Input_14), .alta_operatie(demux_alta_operatie_1_alta_operatie),
    .\final (Output_2));
  numarator_afisor numarator_afisor_1 (
    .clk(clock_1_out), .enable(demux_selectare_operatie_1_enable_afisare), .numar(numarator_afisor_1_numar));
  registru_suma registru_suma_1 (
    .suma_in(undriven), .clk(clock_1_out), .reset(Input_2), .suma_out(registru_suma_1_suma_out));
  mux_afisor mux_afisor_1 (
    .sel(numarator_afisor_1_numar), .c1(transformator_cifre_1_mii), .c2(transformator_cifre_1_sute),
    .c3(transformator_cifre_1_zeci), .c4(transformator_cifre_1_unitati), .catod(mux_afisor_1_catod));
  scazator_bancnote scazator_bancnote_1 (
    .bancnote_retrase(algoritm_bancnote_1_b500_out), .validare(uc_1_enable_scazator500),
    .bancnote_initiale(memorie_bancnote_1_nr500_curent),
    .bancnote_finale(scazator_bancnote_1_bancnote_finale), .\final (scazator_bancnote_1_final));
  scazator_bancnote scazator_bancnote_2 (
    .bancnote_retrase(algoritm_bancnote_1_b100_out), .validare(uc_1_enable_scazator100),
    .bancnote_initiale(memorie_bancnote_1_nr100_nou), .bancnote_finale(scazator_bancnote_2_bancnote_finale),
    .\final (scazator_bancnote_2_final));
  scazator_bancnote scazator_bancnote_3 (
    .bancnote_retrase(algoritm_bancnote_1_b50_out), .validare(uc_1_enable_scazator50),
    .bancnote_initiale(memorie_bancnote_1_nr50_nou), .bancnote_finale(scazator_bancnote_3_bancnote_finale),
    .\final (scazator_bancnote_3_final));
  scazator_bancnote scazator_bancnote_4 (
    .bancnote_retrase(algoritm_bancnote_1_b10_out), .validare(uc_1_enable_scazator10),
    .bancnote_initiale(memorie_bancnote_1_nr10nou), .bancnote_finale(scazator_bancnote_4_bancnote_finale),
    .\final (scazator_bancnote_4_final));
  scazator_sold scazator_sold_1 (
    .suma_retrasa(transformator_suma_1_suma), .validare(uc_1_enable_scazator),
    .suma_initiala(registru_suma_1_suma_out), .suma_finala(scazator_sold_1_suma_finala),
    .final_scazator(scazator_sold_1_final_scazator));
  decodificator_afisor decodificator_afisor_1 (
    .cifra(mux_afisor_1_catod), .afis(Output_bus_1), .\final (decodificator_afisor_1_final));
  mux_anod mux_anod_1 (.sel(numarator_afisor_1_numar), .anod(Output_bus_2));
endmodule

// VHDL entity debouncer, as the project stores it:
LIBRARY ieee;
USE ieee.std_logic_1164.all;

ENTITY debouncer IS
  PORT (
  	clk, s_in: in std_logic;
  	s_out: out std_logic
    );
END debouncer;

--------------------------------------------------------------------------------
--Complete your VHDL description below
--------------------------------------------------------------------------------

ARCHITECTURE arch_debouncer OF debouncer IS

signal delay1, delay2, delay3: std_logic;
BEGIN
	PROCESS(clk)
	BEGIN
		IF (clk'event and clk = '1') THEN
			delay1 <= s_in;
			delay2 <= delay1;
			delay3 <= delay2;
		END IF;
	END PROCESS;
	s_out <= delay1 and delay2 and delay3;

END arch_debouncer;

// VHDL entity registru_incarcare_pin, as the project stores it:
LIBRARY ieee;
USE ieee.std_logic_1164.all;

ENTITY registru_incarcare_pin IS
  PORT (
 		pin_in: in std_logic_vector(3 downto 0);
 		enable, clk, reset: in std_logic;
 		pin_out: out std_logic_vector(3 downto 0)		
    );
END registru_incarcare_pin;



ARCHITECTURE arch_registru_pin OF registru_incarcare_pin IS

signal valoare: std_logic_vector(3 downto 0);

BEGIN
process( pin_in, clk)
begin
	if( enable = '1') then
	if( reset = '1') then
		valoare <= "0000";
	elsif( clk = '1' and clk'event) then
		valoare <= pin_in;
	end if;
	end if;
end process;

pin_out <= valoare;

END arch_registru_pin;

// VHDL entity registru_actualizare_bancnote, as the project stores it:
LIBRARY ieee;
USE ieee.std_logic_1164.all;

ENTITY registru_actualizare_bancnote IS
  PORT (
 		bancnote_in: in std_logic_vector(3 downto 0);
 		clk, reset, enable: in std_logic;
 		bancnote_out: out std_logic_vector(3 downto 0);
 		validare: in std_logic
    );
END registru_actualizare_bancnote;



ARCHITECTURE arch_registru_bancnote OF registru_actualizare_bancnote IS

signal valoare: std_logic_vector(3 downto 0);
BEGIN

process(clk, bancnote_in, enable, validare, reset)
begin
	if(enable = '1') then
	if (reset = '1') then
		valoare <= "0000";
	elsif(clk = '1' and clk'event and validare= '1') then
		valoare <= bancnote_in;
	end if;
	end if;
end process;

bancnote_out <= valoare;
END arch_registru_bancnote;

// VHDL entity registru_suma, as the project stores it:
LIBRARY ieee;
USE ieee.std_logic_1164.all;

ENTITY registru_suma IS
  PORT (
 		suma_in: in std_logic_vector(9 downto 0);
 		clk, reset: in std_logic;
 		suma_out: out std_logic_vector(9 downto 0)
    );
END registru_suma;



ARCHITECTURE arch_registru_suma OF registru_suma IS

signal valoare: std_logic_vector(9 downto 0);
BEGIN

process(clk, suma_in)
begin
	if (reset = '1') then
		valoare <= "0000000000";
	elsif(clk = '1' and clk'event) then
		valoare <= suma_in;
	end if;

end process;

suma_out <= valoare;
END arch_registru_suma;

// VHDL entity numarator_bancnote, as the project stores it:
LIBRARY ieee;
USE ieee.std_logic_1164.all;
USE ieee.std_logic_unsigned.all;

ENTITY numarator_bancnote IS
  PORT (
 		clk, enable, reset: in std_logic;
 		numar: out std_logic_vector(3 downto 0)
 		
    );
END numarator_bancnote;



ARCHITECTURE arch_numarator OF numarator_bancnote IS

signal valoare: std_logic_vector(3 downto 0);

BEGIN

process( clk, enable, reset)

begin
	if (reset = '1') then
		valoare <= "0000";
	elsif (enable = '1') then
			if (clk = '1' and clk'event) then
				if( valoare < "1111") then
					valoare <= valoare + "0001";
				else 
					valoare <= "0000";
				end if;
			end if;
	end if;
end process;

numar <= valoare;

END arch_numarator;

// VHDL entity demux_alta_operatie, as the project stores it:
LIBRARY ieee;
USE ieee.std_logic_1164.all;

ENTITY demux_alta_operatie IS
  PORT (
 		enable: in std_logic;
 		sel: in std_logic;
 		alta_operatie, final: out std_logic
    );
END demux_alta_operatie;



ARCHITECTURE arch_demux OF demux_alta_operatie IS

signal operatie, fin: std_logic;
BEGIN
process(enable, sel)
begin
	if(enable = '1') then
	if( sel = '1') then
		operatie <= '1';
		fin <= '0';
	else
		operatie <= '0';
		fin <= '1';
	end if;
	end if;
end process;

alta_operatie <= operatie;
final <= fin;

END arch_demux;

// VHDL entity demux_selectare_operatie, as the project stores it:
LIBRARY ieee;
USE ieee.std_logic_1164.all;

ENTITY demux_selectare_operatie IS
  PORT (
  		
  		sel: in std_logic_vector(1 downto 0);
  		enable: in std_logic;
  		validare: in std_logic;
  		enable_afisare, enable_depunere, enable_retragere, enable_schimbare: out std_logic
    );
END demux_selectare_operatie;



ARCHITECTURE arch_demux OF demux_selectare_operatie IS

signal enable_a, enable_d, enable_r, enable_s: std_logic;

BEGIN
process( enable, sel, validare)
begin
	if(enable = '1' and validare = '1') then
		case sel is
			when "00" => enable_a <= '1';
					   enable_d <= '0';
					   enable_r <= '0';
					   enable_s <= '0';
			when "01" => enable_a <= '0';
					   enable_d <= '1';
					   enable_r <= '0';
					   enable_s <= '0';
			when "10" => enable_a <= '0';
					   enable_d <= '0';
					   enable_r <= '1';
					   enable_s <= '0';
			when "11" => enable_a <= '0';
					   enable_d <= '0';
					   enable_r <= '0';
					   enable_s <= '1';
			when others => enable_a <= '0';
					   	enable_d <= '0';
					   	enable_r <= '0';
					   	enable_s <= '0';
		end case;
	end if;
end process;

enable_afisare <= enable_a;
enable_depunere <= enable_d;
enable_retragere <= enable_r;
enable_schimbare <= enable_s;

END arch_demux;

// VHDL entity sumator_sold, as the project stores it:
LIBRARY ieee;
USE ieee.std_logic_1164.all;
use ieee.std_logic_unsigned.all;
use ieee.std_logic_arith.all;

ENTITY sumator_sold IS
  PORT (
 		suma_depusa: in std_logic_vector(9 downto 0);
 		validare: in std_logic;
 		suma_initiala: in std_logic_vector(9 downto 0);
 		suma_finala: out std_logic_vector(9 downto 0);
 		final_sumator: out std_logic
    );
END sumator_sold;



ARCHITECTURE arch_sumator OF sumator_sold IS

signal suma_depusa_in, suma_initiala_in, suma_finala_in: integer;

BEGIN

process(suma_depusa, suma_initiala, validare)

begin
	
	if(validare = '1') then
		suma_depusa_in <= conv_integer(suma_depusa);
		suma_initiala_in <= conv_integer(suma_initiala);
		suma_finala_in <= suma_depusa_in + suma_initiala_in;
		final_sumator <= '1';
	end if;

end process;

suma_finala <= conv_std_logic_vector(suma_finala_in, 10);

END arch_sumator;

// VHDL entity scazator_sold, as the project stores it:
LIBRARY ieee;
USE ieee.std_logic_1164.all;

use ieee.std_logic_unsigned.all;
use ieee.std_logic_arith.all;

ENTITY scazator_sold IS
  PORT (
 		suma_retrasa: in std_logic_vector(9 downto 0);
 		validare: in std_logic;
 		suma_initiala: in std_logic_vector(9 downto 0);
 		suma_finala: out std_logic_vector(9 downto 0);
 		final_scazator: out std_logic
    );
END scazator_sold;



ARCHITECTURE arch_scazator OF scazator_sold IS

signal suma_retrasa_in, suma_initiala_in, suma_finala_in: integer;

BEGIN

process(suma_retrasa, suma_initiala, validare)

begin
	
	if(validare = '1') then
		suma_retrasa_in <= conv_integer(suma_retrasa);
		suma_initiala_in <= conv_integer(suma_initiala);
		suma_finala_in <= suma_initiala_in - suma_retrasa_in;
		final_scazator <= '1';
	end if;

end process;

suma_finala <= conv_std_logic_vector(suma_finala_in, 10);

END arch_scazator;

// VHDL entity comparator_suma, as the project stores it:
LIBRARY ieee;
USE ieee.std_logic_1164.all;
use ieee.std_logic_unsigned.all;
use ieee.std_logic_arith.all;

ENTITY comparator_suma IS
  PORT (
  		suma_retragere: in std_logic_vector(9 downto 0);
  		suma_cont: in std_logic_vector(9 downto 0);
  		enable: in std_logic;
  		confirmare: out std_logic
    );
END comparator_suma;



ARCHITECTURE arch_comparator OF comparator_suma IS

signal suma_retragere_int, suma_cont_int: integer;
signal confirm: std_logic;

BEGIN
process(suma_retragere, suma_cont, enable)
begin
	if( enable = '1') then
		suma_retragere_int <= conv_integer(suma_retragere);
		suma_cont_int <= conv_integer(suma_cont);
		if (suma_retragere > suma_cont_int) then
			confirm <= '0';
		else	 
			confirm <= '1';
		end if;
	end if;

end process;

confirmare <= confirm;
END arch_comparator;

// VHDL entity comparator_bancnote, as the project stores it:
LIBRARY ieee;
USE ieee.std_logic_1164.all;

use ieee.std_logic_unsigned.all;
use ieee.std_logic_arith.all;

ENTITY comparator_bancnote IS
  PORT (
  		nr_bancnote: in std_logic_vector(3 downto 0);
  		bancnote_disponibile: in std_logic_vector(3 downto 0);
  		enable: in std_logic;
  		confirmare: out std_logic
    );
END comparator_bancnote;



ARCHITECTURE arch_comparator OF comparator_bancnote IS

signal nr_bancnote_int, bancnote_disponibile_int: integer;
signal confirm: std_logic;

BEGIN

process(nr_bancnote, bancnote_disponibile, enable)
begin
	if( enable = '1') then
		 nr_bancnote_int <= conv_integer(nr_bancnote);
		 bancnote_disponibile_int <= conv_integer(bancnote_disponibile);
		if (nr_bancnote_int > bancnote_disponibile_int) then
			confirm <= '0';
		else	 
			confirm <= '1';
		end if;
	end if;

end process;

confirmare <= confirm;
END arch_comparator;

// VHDL entity memorie_cont, as the project stores it:
LIBRARY ieee;
USE ieee.std_logic_1164.all;
USE ieee.std_logic_unsigned.all;


ENTITY memorie_cont IS
  PORT (
  		 pin_vechi: in std_logic_vector(3 downto 0);
		 clk: in std_logic;
		 enable_schimbare_pin, enable_adunare_sold, enable_scadere_sold, enable_transmitere_sold: in std_logic;
		 suma_adunare, suma_scadere: in std_logic_vector(9 downto 0);
		 pin_nou: in std_logic_vector(3 downto 0);
		 sold: out std_logic_vector(9 downto 0);
		 final_mem_sc, final_mem_ad, final_mem_schimbare: out std_logic;
		 validare_pin: in std_logic
 		
    );
END memorie_cont;



ARCHITECTURE arch_memorie OF memorie_cont IS

type memorie is array(15 downto 0) of std_logic_vector(13 downto 0);
signal M: memorie:= (
     "00000000001110",    	
	"00010101101110",		
	"00100010011110",
	"00110111010100",
	"01000000111010",
	"01010111100101",
	"01100101011011",
	"01110001110111",
	"10000011110110",
	"10010111000110",
	"10100000111001",
	"10110110111100",
	"11000011110100",
	"11010100000010",
	"11100101001000",
	"11110111110101"
	 ); 
BEGIN

process(validare_pin, clk, pin_vechi, enable_schimbare_pin, enable_adunare_sold, enable_scadere_sold, enable_transmitere_sold, pin_nou, suma_adunare, suma_scadere)
begin 
	if(clk = '1' and clk'event) then
		if(enable_schimbare_pin = '1' and validare_pin = '1') then
			M(conv_integer(pin_vechi))(13 downto 10) <= pin_nou;
			final_mem_schimbare <= '1';
		elsif (enable_adunare_sold = '1') then
				M(conv_integer(pin_vechi))(9 downto 0) <= suma_adunare;
				final_mem_ad <= '1';
		elsif (enable_scadere_sold = '1') then
				M(conv_integer(pin_vechi))(9 downto 0) <= suma_scadere;
				final_mem_sc <= '1';
		elsif (enable_transmitere_sold = '1') then
				sold <= M(conv_integer(pin_vechi))(9 downto 0);
		end if;
		
					
	end if;
end process;

END arch_memorie;

// VHDL entity memorie_bancnote, as the project stores it:
LIBRARY ieee;
USE ieee.std_logic_1164.all;

USE ieee.std_logic_unsigned.all;

ENTITY memorie_bancnote IS
  PORT (
		
		 clk: in std_logic;
		 enable_adunare, enable_scadere, enable_transmitere: in std_logic;
		 nr500_ad, nr100_ad, nr50_ad, nr10_ad: in std_logic_vector(3 downto 0);
		 nr500_sc, nr100_sc, nr50_sc, nr10_sc: in std_logic_vector(3 downto 0);
		 nr500_curent, nr100_nou, nr50_nou, nr10nou: out std_logic_vector(3 downto 0);
		 final_mem_ad,  final_mem_sc, final_tr: out std_logic
    );
END memorie_bancnote;



ARCHITECTURE arch_memorie OF memorie_bancnote IS

type memorie is array(3 downto 0) of std_logic_vector(3 downto 0);
signal M: memorie:= (
    	"1010",
    	"1010",
    	"1010",
    	"1010"
	 ); 
BEGIN

process(clk,  enable_adunare, enable_scadere, enable_transmitere)
begin 
	if( clk = '1' and clk'event) then
		if( enable_adunare = '1') then
			M(0) <= nr500_ad;
			M(1) <= nr100_ad;
			M(2) <= nr50_ad;
			M(3) <= nr10_ad;
			final_mem_ad <= '1';
		elsif ( enable_scadere = '1') then
				M(0) <= nr500_sc;
				M(1) <= nr100_sc;
				M(2) <= nr50_sc;
				M(3) <= nr10_sc;
				final_mem_sc <= '1';
		elsif (enable_transmitere = '1') then
				 nr500_curent <= M(0);
				 nr100_nou <= M(1);
				 nr50_nou <= M(2);
				 nr10nou <= M(3);
				 final_tr <= '1';
		end if;	
		
	end if;
end process;


END arch_memorie;

// VHDL entity afisor_suma, as the project stores it:
LIBRARY ieee;
USE ieee.std_logic_1164.all;
use IEEE.STD_LOGIC_UNSIGNED.all; 

ENTITY afisor_suma IS
  PORT (
  		
		cifra1, cifra2, cifra3, cifra4: in std_logic_vector(3 downto 0);
  		clk: in std_logic;
  		anod: out std_logic_vector(3 downto 0);
  		catod: out std_logic_vector(6 downto 0);
  		final: out std_logic
    );
END afisor_suma;


ARCHITECTURE arch_afisor OF afisor_suma IS

signal numar: std_logic_vector (15 downto 0);
signal an: std_logic_vector (3 downto 0);

BEGIN

PROCESS(clk)
	BEGIN
	 	IF (clk'event and Clk='1') THEN
	 		Numar <= Numar + 1;
	 	END IF; 	
END PROCESS;


PROCESS(clk, cifra1, cifra2, cifra3, cifra4)
	BEGIN
	 	IF (clk'event and clk='1') THEN
	 		  case (Numar(15 downto 14)) is
        			when "00" => An<=Cifra1; Anod<="1110";
        			when "01" => An<=Cifra2; Anod<="1101";
        			when "10" => An<=Cifra3; Anod<="1011";
        			when "11" => An<=Cifra4; Anod<="0111";
        			when others => An<="1111"; Anod<="0000";
    			end case;

	 	END IF; 	
END PROCESS;

PROCESS(Clk)
BEGIN
    IF (Clk'event and Clk='1') THEN
        case (An) is
                when "0001" => Catod<="1111001";	  
                when "0010" => Catod<="0100100";	 
                when "0011" => Catod<="0110000";	  
                when "0100" => Catod<="0011001";	  
                when "0101" => Catod<="0010010";	  
                when "0110" => Catod<="0000010";	  
                when "0111" => Catod<="1111000";	  
                when "1000" => Catod<="0000000";	  
                when "1001" => Catod<="0010000";	  
                when "1010" => Catod<="0001000";	  
                when "1011" => Catod<="0000011";	  
                when "1100" => Catod<="1000110";	  
                when "1101" => Catod<="0100001";	  
                when "1110" => Catod<="0000110";	  
                when "1111" => Catod<="0001110";	  
                when others => Catod<="1000000";	  
        end case;
    end if;
    final <= '1';
end process;

END arch_afisor;

// VHDL entity transformator_suma, as the project stores it:
LIBRARY ieee;
USE ieee.std_logic_1164.all;
use ieee.std_logic_unsigned.all;
use ieee.std_logic_arith.all;

ENTITY transformator_suma IS
  PORT (
 		mii, sute, zeci, unitati: in std_logic_vector(3 downto 0);
 		enable: in std_logic;
 		suma: out std_logic_vector(9 downto 0);
 		final_trans_suma: out std_logic;
 		validare: in std_logic
 		
    );
END transformator_suma;



ARCHITECTURE arch_transformator OF transformator_suma IS

signal suma_in, mii_in, sute_in, zeci_in, unitati_in: integer :=0;
BEGIN
process(enable, mii, sute, zeci, unitati, validare)
begin

	if( enable = '1' and validare = '1') then
		mii_in <= conv_integer(mii);
		sute_in <= conv_integer(sute);
		zeci_in <= conv_integer(zeci);
		unitati_in <= conv_integer(unitati);
		suma_in <= mii_in*1000 + sute_in*100 +zeci_in*10 +unitati_in;
		final_trans_suma <= '1';
		
	end if;
end process;

suma <= conv_std_logic_vector(suma_in, 10);


END arch_transformator;

// VHDL entity uc, as the project stores it:
LIBRARY ieee;
USE ieee.std_logic_1164.all;

ENTITY uc IS
  PORT (
 		clk, reset, start: in std_logic;
 		final_mem_banc_sc, enable_alta_op, final_schimbare, final_sc_banc500, final_sc_banc100, final_sc_banc50, final_sc_banc10, fin_mem_sc, confirm_algoritm, final_transmitere, confirm_comparator, final_numarare500, final_numarare100, final_numarare50, final_numarare10: in std_logic; 
 		final_scazator_sold, final_mem_banc_ad, final_mem_ad, final_sumator_banc500, final_sumator_banc100, final_sumator_banc50, final_sumator_banc10: in std_logic;
 		final_sumator_sold, final_trans_suma_sc, final_trans_suma_ad, validare_pin, finalizare_sel_op, enable_afisare, enable_depunere, enable_retragere, enable_schimbare, finalizare_afisare: in std_logic;
 		led_final, enable_demux_alta_op, enable_scadere_banc, enable_scazator500, enable_scazator100, enable_scazator50, enable_scazator10, enable_scadere_sold, enable_scazator, enable_algoritm, enable_transmitere, enable_comparator,enable_adunare_banc, enable_pin, enable_suma, enable_adunare_sold, enable_operatie, enable_sum500, enable_sum100, enable_sum50, enable_sum10: out std_logic;
 		enable_nr500, enable_nr100, enable_nr50, enable_nr10: out std_logic
    );
END uc;



ARCHITECTURE arch_uc OF uc IS

type stari is (asteapta, introducere_pin, alegere_operatie, afisare_sold, urmatoarea_operatie, depunere_numerar, depunere_bancnote, retragere_numerar, eliberare_bancnote, schimbare_pin, finalizare);
signal stare, nxt_stare: stari;

BEGIN

actualizare_stare: process(reset, clk)

	begin
		if(reset = '1') then
			stare<= asteapta;
		elsif clk'event and clk = '1' then
			stare <= nxt_stare; 
		end if;
	end process;

tranzitii: process(stare, clk, reset, start,final_mem_banc_sc, enable_alta_op, final_schimbare, final_sc_banc500, final_sc_banc100, final_sc_banc50, final_sc_banc10, fin_mem_sc, confirm_algoritm, final_transmitere, confirm_comparator, final_numarare500, final_numarare100, final_numarare50, final_numarare10 ,final_scazator_sold, final_mem_banc_ad, final_mem_ad, final_sumator_banc500, final_sumator_banc100, final_sumator_banc50, final_sumator_banc10,final_sumator_sold, final_trans_suma_sc, final_trans_suma_ad, validare_pin, finalizare_sel_op, enable_afisare, enable_depunere, enable_retragere, enable_schimbare, finalizare_afisare)

	begin		

	case stare is
	
		when asteapta =>
			led_final <= '0';
			enable_demux_alta_op <= '0';
			enable_scadere_banc <= '0';
			enable_scazator500 <= '0';
			enable_scazator100 <= '0';
			enable_scazator50 <= '0';
			enable_scazator10 <= '0';
			enable_scadere_sold <= '0';
			enable_scazator <= '0';
			enable_algoritm <= '0';
			enable_transmitere <= '0';
			enable_comparator <= '0';
			enable_adunare_banc <= '0';
			enable_pin <= '0';
			enable_suma <= '0';
			enable_adunare_sold <= '0';
			enable_operatie <= '0';
			enable_sum500 <= '0';
			enable_sum100 <= '0';
			enable_sum50 <= '0';
			enable_sum10 <= '0';
			enable_nr500 <= '0';
			enable_nr100 <= '0';
			enable_nr50 <= '0';
			enable_nr10 <= '0';
			if (start = '1') then
				enable_pin <= '1';
				nxt_stare <= introducere_pin;
			else
				nxt_stare <= asteapta;
			end if;

		when introducere_pin =>
			if (validare_pin = '1') then
				enable_operatie <= '1';
				nxt_stare <= alegere_operatie;
			else 
				nxt_stare <= introducere_pin;
			end if;
			
		when alegere_operatie =>
			if (finalizare_sel_op = '1') then
				if (enable_afisare = '1' ) then
					nxt_stare <=afisare_sold;
				
				elsif (enable_depunere = '1' ) then
					nxt_stare <=depunere_numerar;
				
				elsif (enable_retragere = '1' ) then
					nxt_stare <=retragere_numerar;
				
				elsif ( enable_schimbare = '1' ) then
					nxt_stare <=schimbare_pin;
	 
				 else
				     nxt_stare <=alegere_operatie;
				  end if;
			end if;

		when afisare_sold =>
			if (finalizare_afisare = '1') then
				enable_demux_alta_op <= '1';
				nxt_stare <= urmatoarea_operatie;
			else nxt_stare <= afisare_sold;
			end if;
			
		when depunere_numerar =>
			if(final_trans_suma_ad = '1') then
				enable_suma <= '1';
				if ( final_sumator_sold = '1') then
					enable_adunare_sold <= '1';
					if (final_mem_ad = '1') then
						enable_nr500 <= '1';
						enable_nr100 <= '1';
						enable_nr50 <= '1';
						enable_nr10 <= '1';
						nxt_stare <= depunere_bancnote;
					else 
						nxt_stare <=depunere_numerar;
					end if;
				end if;
			end if;
				

		when depunere_bancnote =>
			if(final_numarare500 = '1') then
				enable_sum500 <= '1';
			end if;

			if(final_numarare100 = '1') then
				enable_sum100 <= '1';
			end if;

			if(final_numarare50 = '1') then
				enable_sum50 <= '1';
			end if;

			if(final_numarare10 = '1') then
				enable_sum10 <= '1';
			end if;
			
			if (final_sumator_banc500 = '1' and final_sumator_banc100 = '1' and final_sumator_banc50 = '1' and final_sumator_banc10 = '1') then
					enable_adunare_banc <= '1';
			end if;
			
			if(final_mem_banc_ad = '1') then
				enable_demux_alta_op <= '1';
				nxt_stare <= urmatoarea_operatie;
			else nxt_stare <= depunere_bancnote;
			end if;

		when retragere_numerar =>
			if(final_trans_suma_sc = '1' ) then
				enable_comparator <= '1';
				if( confirm_comparator = '1') then
					enable_transmitere <= '1';
	    					if( final_transmitere = '1') then
	    						enable_algoritm <= '1';
	    						if (confirm_algoritm = '1') then
	    							nxt_stare <= eliberare_bancnote;
	    								else nxt_stare <= retragere_numerar;
							end if;
						end if;
				end if;
			end if;


							
		
	    when eliberare_bancnote =>
	    		enable_scazator <= '1';
				if( final_scazator_sold = '1') then
					enable_scadere_sold <= '1';
						if( fin_mem_sc = '1') then
							enable_scazator500 <= '1';
							enable_scazator100 <= '1';
							enable_scazator50 <= '1';
							enable_scazator10 <= '1';
							if (final_sc_banc500 = '1' and final_sc_banc100 = '1' and final_sc_banc50 = '1' and final_sc_banc10 = '1') then
									enable_scadere_banc <= '1';
									if(final_mem_banc_sc = '1') then
										enable_demux_alta_op <= '1';
										nxt_stare <= urmatoarea_operatie;
									else nxt_stare <= eliberare_bancnote;
									end if;
							end if;
						end if;
				end if;
							
									
	    	when schimbare_pin =>
	    		if (final_schimbare = '1') then
	    			enable_demux_alta_op <= '1';
	    			nxt_stare <= urmatoarea_operatie;
	    			
	    		end if;
	    			
		when urmatoarea_operatie =>
			if ( enable_alta_op = '1') then
				nxt_stare <= asteapta;
			else 
				nxt_stare <= finalizare;
			end if;

		when finalizare =>
			led_final <= '1';
			
	end case;				
	end process;
	
END arch_uc;

// VHDL entity algoritm_bancnote, as the project stores it:
LIBRARY ieee;
USE ieee.std_logic_1164.all;
use ieee.std_logic_unsigned.all;
use ieee.std_logic_arith.all;


ENTITY algoritm_bancnote IS
  PORT (
  		suma: in std_logic_vector(9 downto 0);
  		enable: in std_logic;
  		b500_in, b100_in, b50_in, b10_in: in std_logic_vector(3 downto 0);
  		b500_out, b100_out, b50_out, b10_out: out std_logic_vector(3 downto 0);
  		confirm: out std_logic
    );
END algoritm_bancnote;



ARCHITECTURE arch_algoritm OF algoritm_bancnote IS

signal b500_int, b100_int, b50_int, b10_int, b500_outt, b100_outt, b50_outt, b10_outt, suma_int, total: integer:=0;
signal confirmare: std_logic;
BEGIN
process( suma, enable, b500_in, b100_in, b50_in, b10_in)
begin
	suma_int <= conv_integer(suma);
	b500_int <= conv_integer(b500_in);
	b100_int <= conv_integer(b100_in);
	b50_int <= conv_integer(b50_in);
	b10_int <= conv_integer(b10_in);
	total <= 10;
	while (suma_int > 0 and total > 0) loop
		if ( b500_int > 0 and suma_int-500 > -1) then
			b500_outt <= b500_outt + 1;
			suma_int <= suma_int - 500;
		elsif ( b100_int > 0 and suma_int-100 > -1) then
			b100_outt <= b100_outt + 1;
			suma_int <= suma_int - 100;
		elsif ( b50_int > 0 and suma_int-50 > -1) then
			b50_outt <= b50_outt + 1;
			suma_int <= suma_int - 50;
		elsif ( b10_int > 0 and suma_int-10 > -1) then
			b10_outt <= b10_outt + 1;
			suma_int <= suma_int - 10;	
		end if;
		total <= total - 1;
	end loop;
	if (total = 0) then
		confirmare <= '0';
	else 
		confirmare <= '1';
	end if;
	
		
end process;

b500_out <= conv_std_logic_vector(b500_outt, 4);
b100_out <= conv_std_logic_vector(b100_outt, 4);
b50_out <= conv_std_logic_vector(b50_outt, 4);
b10_out <= conv_std_logic_vector(b10_outt, 4);
confirm <= confirmare;

END arch_algoritm;

// VHDL entity transformator_cifre, as the project stores it:
LIBRARY ieee;
USE ieee.std_logic_1164.all;

use ieee.std_logic_unsigned.all;
use ieee.std_logic_arith.all;

ENTITY transformator_cifre IS
  PORT (
 		
 		suma: in std_logic_vector(9 downto 0);
 		enable: in std_logic;
 		mii, sute, zeci, unitati: out std_logic_vector(3 downto 0)
 		
    );
END transformator_cifre;



ARCHITECTURE arch_transformator OF transformator_cifre IS

signal suma_in, mii_in, sute_in, zeci_in, unitati_in: integer :=0;
BEGIN

process(enable, suma)
begin

	if( enable = '1') then
		suma_in <= conv_integer(suma);
		mii_in <= suma_in/1000;
		sute_in <= (suma_in/100) mod 10;
		zeci_in <= (suma_in/10) mod 10;
		unitati_in <= suma_in mod 10;
		
	end if;

end process;

mii <= conv_std_logic_vector(mii_in, 4);
sute <= conv_std_logic_vector(sute_in, 4);
zeci <= conv_std_logic_vector(zeci_in, 4);
unitati <= conv_std_logic_vector(unitati_in, 4);

END arch_transformator;

// VHDL entity sumator_bancnote, as the project stores it:
LIBRARY ieee;
USE ieee.std_logic_1164.all;

use ieee.std_logic_unsigned.all;
use ieee.std_logic_arith.all;

ENTITY sumator_bancnote IS
  PORT (
 		bancnote_depuse: in std_logic_vector(3 downto 0);
 		validare: in std_logic;
 		bancnote_initiale: in std_logic_vector(3 downto 0);
 		bancnote_finale: out std_logic_vector(3 downto 0);
 		final: out std_logic
    );
END sumator_bancnote;



ARCHITECTURE arch_sumator OF sumator_bancnote IS

signal bancnote_depuse_in, bancnote_initiale_in, bancnote_finale_in: integer;

BEGIN

process(bancnote_depuse, bancnote_initiale, validare)

begin
	
	if(validare = '1') then
		bancnote_depuse_in <= conv_integer(bancnote_depuse);
		bancnote_initiale_in <= conv_integer(bancnote_initiale);
		bancnote_finale_in <= bancnote_depuse_in + bancnote_initiale_in;
		final <= '1';
	end if;

end process;

bancnote_finale <= conv_std_logic_vector(bancnote_finale_in, 4);

END arch_sumator;

// VHDL entity scazator_bancnote, as the project stores it:
LIBRARY ieee;
USE ieee.std_logic_1164.all;

use ieee.std_logic_unsigned.all;
use ieee.std_logic_arith.all;

ENTITY scazator_bancnote IS
  PORT (
 		bancnote_retrase: in std_logic_vector(3 downto 0);
 		validare: in std_logic;
 		bancnote_initiale: in std_logic_vector(3 downto 0);
 		bancnote_finale: out std_logic_vector(3 downto 0);
 		final: out std_logic
    );
END scazator_bancnote;



ARCHITECTURE arch_scazator OF scazator_bancnote IS

signal bancnote_retrase_in, bancnote_initiale_in, bancnote_finale_in: integer;

BEGIN

process(bancnote_retrase, bancnote_initiale, validare)

begin
	
	if(validare = '1') then
		bancnote_retrase_in <= conv_integer(bancnote_retrase);
		bancnote_initiale_in <= conv_integer(bancnote_initiale);
		bancnote_finale_in <= bancnote_initiale_in - bancnote_retrase_in;
		final <= '1';
	end if;

end process;

bancnote_finale <= conv_std_logic_vector(bancnote_finale_in, 4);

END arch_scazator;

// VHDL entity decodificator_afisor, as the project stores it:
LIBRARY ieee;
USE ieee.std_logic_1164.all;

ENTITY decodificator_afisor IS
  PORT (
 	cifra: in std_logic_vector(3 downto 0);
  	afis: out std_logic_vector(6 downto 0);
  	final: out std_logic
    );
END decodificator_afisor;



ARCHITECTURE arch_decod OF decodificator_afisor IS

BEGIN
process(cifra)
	begin
	case cifra is
	when "0000" => afis <= "1111110";
	when "0001" => afis <= "0110000";
	when "0010" => afis <= "1101101";
	when "0011" => afis <= "1111001";
	when "0100" => afis <= "0110011";
	when "0101" => afis <= "1011011";
	when "0110" => afis <= "1111101";
	when "0111" => afis <= "1110000";
	when "1000" => afis <= "1111111";
	when "1001" => afis <= "1111011";
	when others => afis <= "0000000";
end case;
final <= '1';
end process;
end arch_decod;

// VHDL entity numarator_afisor, as the project stores it:
LIBRARY ieee;
USE ieee.std_logic_1164.all;
USE ieee.std_logic_unsigned.all;
USE ieee.std_logic_arith.all;

ENTITY numarator_afisor IS
  PORT (
		clk, enable :in std_logic;
	   	numar: out std_logic_vector(1 downto 0)
    );
END numarator_afisor;



ARCHITECTURE arch_numarator OF numarator_afisor IS

BEGIN
process(clk, enable)
variable count: std_logic_vector(15 downto 0) := "0000000000000000";
begin
	if(enable = '1') then
		if(clk = '1') then
			count := count + 1;
		end if;
		if(count = "1111111111111111") then
		 count := "0000000000000000";
		end if;
	end if;
	numar <= count(15 downto 14);
end process;
end arch_numarator;

// VHDL entity mux_anod, as the project stores it:
LIBRARY ieee;
USE ieee.std_logic_1164.all;

ENTITY mux_anod IS
  PORT (
	   sel : in std_logic_vector(1 downto 0);
  	   anod: out std_logic_vector(3 downto 0)
    );
END mux_anod;



ARCHITECTURE arch_mux OF mux_anod IS

BEGIN
process(sel)
begin
	if( sel = "00") then
		anod <= "1110";
	elsif (sel = "01") then
			anod <= "1101";
		elsif (sel = "10") then
				anod <= "1011";
				elsif (sel = "11") then
					anod <= "0111";
				end if; 
end process;
END arch_mux;

// VHDL entity mux_afisor, as the project stores it:
LIBRARY ieee;
USE ieee.std_logic_1164.all;

ENTITY mux_afisor IS
  PORT (
	   sel : in std_logic_vector(1 downto 0);
  	   c1, c2, c3, c4: in std_logic_vector(3 downto 0);
  	   catod: out std_logic_vector(3 downto 0)
    );
END mux_afisor;



ARCHITECTURE arch_mux OF mux_afisor IS

BEGIN
process(sel, c1, c2, c3, c4)
begin
 	if( sel = "00") then
		catod <= c1;
	elsif (sel = "01") then
			catod <= c2;
		elsif (sel = "10") then
				catod <= c3;
				elsif (sel = "11") then
					catod <= c4;
				end if; 

end process;
END arch_mux;

// VHDL entity div_frecventa, as the project stores it:
LIBRARY ieee;
USE ieee.std_logic_1164.all;

USE ieee.std_logic_unsigned.all;

ENTITY div_frecventa IS
  PORT (
  CLK_100: IN std_logic;
  RESET: IN std_logic;
  CLK_1: OUT std_logic
    );
END div_frecventa;



ARCHITECTURE TypeArchitecture OF div_frecventa IS

Component counter
 PORT(
 CLK: IN std_logic;
 RESET: IN std_logic;
 COUT: OUT std_logic
 );
 END component;
 Component tflipflop
PORT(
T,CLK: IN std_logic;
Q: OUT std_logic
);
end component;
signal N1: std_logic;
BEGIN
C1: counter port map(CLK_100,RESET,N1);
C2: tflipflop port map('1',N1,CLK_1);
END TypeArchitecture;


LIBRARY ieee;
USE ieee.std_logic_1164.all;
USE ieee.std_logic_unsigned.all;

ENTITY counter is
 PORT(
 CLK: IN std_logic;
 RESET: IN std_logic;
 COUT: OUT std_logic
 );
 END counter;

 ARCHITECTURE behavioural OF counter IS
 BEGIN
 process(CLK)
 variable COUNT: std_logic_vector(25 downto 0):=(others=>'0');
 begin
 if rising_edge(CLK) then
 if RESET='1'then 
 count:=(others=>'0');
else
	count:=count+1;
end if;
end if;
if count="10111110101111000010000000" then
COUT <= '1';
count:=(others=>'0');
else COUT <='0';
end if;
end process;
end behavioural;


LIBRARY ieee;
USE ieee.std_logic_1164.all;
USE ieee.std_logic_unsigned.all;

Entity tflipflop is
PORT(
T,CLK: IN std_logic;
Q: OUT std_logic

);
end tflipflop;

ARCHITECTURE behave of tflipflop is
BEGIN
PROCESS(CLK)
variable Qv: std_logic:='0';
begin
if rising_edge(CLK) then
if T='0' then
Qv:=Qv;
else
Qv:=NOT Qv;
end if;
end if;
Q<=Qv;
end process;
end behave;
