// Logisim project memorie_rom_project.circ as structural Verilog
module main (
  input  in_1,
  input  [3:0] in_2,
  output [5:0] out_3
);

  memorie_rom memorie_rom_1 (.CS(in_1), .Addr(in_2), .D_ROM(out_3));
endmodule

// VHDL entity memorie_rom, as the project stores it:
--------------------------------------------------------------------------------
-- Project :
-- File    :
-- Autor   :
-- Date    :
--
--------------------------------------------------------------------------------
-- Description :
--
--------------------------------------------------------------------------------

LIBRARY ieee;
USE ieee.std_logic_1164.all;
USE ieee.std_logic_unsigned.all;

ENTITY memorie_rom IS
  PORT (	
		CS: in std_logic;
		Addr: in std_logic_vector (3 downto 0);
		D_ROM: out std_logic_vector (5 downto 0)
    );
END memorie_rom;

--------------------------------------------------------------------------------
--Complete your VHDL description below
--------------------------------------------------------------------------------

ARCHITECTURE arh_rom OF memorie_rom IS

type ROM_type is array(0 to 15) of std_logic_vector(5 downto 0);
signal ROM_M: ROM_type:=("010101", "110100", "001100", "110111", others => "000001");

BEGIN

D_ROM<=ROM_M(conv_integer(Addr));

END arh_rom;
